// Logisim project sap2_main.circ as structural Verilog: 1 circuit, main circuit main
module main (
  input  in_1,
  input  in_2,
  input  in_3,
  input  in_4,
  input  in_5,
  input  in_6,
  input  in_7,
  input  in_8,
  input  [2:0] in_9,
  input  in_10,
  input  in_11,
  input  in_12,
  input  in_13,
  input  in_14,
  input  in_15,
  input  in_16,
  input  in_17,
  input  in_18,
  input  in_19,
  input  in_20,
  input  in_21,
  input  in_22,
  input  in_23,
  input  in_24,
  input  in_25,
  input  in_26,
  input  in_27,
  input  in_28,
  input  in_29,
  input  in_30,
  input  in_31,
  input  in_32,
  input  in_33,
  input  in_34,
  input  in_35,
  output [15:0] out_36,
  output [15:0] out_37,
  output [15:0] out_38
);

  wire arithmetic_logic_unit_1_p5, arithmetic_logic_unit_1_p7, nor_1_out;
  wire [7:0] ram_1_dout, register_8_1_q1, register_8_2_o1, register_8_3_o1;
  wire [15:0] register_16_1_q1;

  RAM #(.addrWidth(16), .asyncread("true")) ram_1 (
    .addr(register_16_1_q1), .we(in_18), .oe(in_19), .clk(in_20), .din(register_8_1_q1), .dout(ram_1_dout));
  pc pc_1 (.EN(in_4), .LOAD(in_5), .COUNT(in_6), .CLK(in_7), .D_in(out_36), .Q_out(out_36), .O_out(out_37));
  register_16 register_16_1 (
    .D1(out_36[0]), .D2(out_36[1]), .D3(out_36[2]), .D4(out_36[3]), .D5(out_36[4]), .D6(out_36[5]),
    .D7(out_36[6]), .D8(out_36[7]), .D9(out_36[8]), .D10(out_36[9]), .D11(out_36[10]), .D12(out_36[11]),
    .D13(out_36[12]), .D14(out_36[13]), .D15(out_36[14]), .D16(out_36[15]), .LOAD(in_12), .CLK(in_13),
    .EN(in_14), .O1(out_38[0]), .O2(out_38[1]), .O3(out_38[2]), .O4(out_38[3]), .O5(out_38[4]),
    .O6(out_38[5]), .O7(out_38[6]), .O8(out_38[7]), .O9(out_38[8]), .O10(out_38[9]), .O11(out_38[10]),
    .O12(out_38[11]), .O13(out_38[12]), .O14(out_38[13]), .O15(out_38[14]), .O16(out_38[15]),
    .Q1(register_16_1_q1[0]), .Q2(register_16_1_q1[1]), .Q3(register_16_1_q1[2]), .Q4(register_16_1_q1[3]),
    .Q5(register_16_1_q1[4]), .Q6(register_16_1_q1[5]), .Q7(register_16_1_q1[6]), .Q8(register_16_1_q1[7]),
    .Q9(register_16_1_q1[8]), .Q10(register_16_1_q1[9]), .Q11(register_16_1_q1[10]),
    .Q12(register_16_1_q1[11]), .Q13(register_16_1_q1[12]), .Q14(register_16_1_q1[13]),
    .Q15(register_16_1_q1[14]), .Q16(register_16_1_q1[15]));
  register_8 register_8_1 (
    .D1(ram_1_dout[0]), .D2(ram_1_dout[1]), .D3(ram_1_dout[2]), .D4(ram_1_dout[3]), .D5(ram_1_dout[4]),
    .D6(ram_1_dout[5]), .D7(ram_1_dout[6]), .D8(ram_1_dout[7]), .LOAD(in_21), .CLK(in_22), .EN(in_23),
    .Q1(register_8_1_q1[0]), .Q2(register_8_1_q1[1]), .Q3(register_8_1_q1[2]), .Q4(register_8_1_q1[3]),
    .Q5(register_8_1_q1[4]), .Q6(register_8_1_q1[5]), .Q7(register_8_1_q1[6]), .Q8(register_8_1_q1[7]));  // open: O1, O2, O3, O4, O5, O6, O7, O8
  Demultiplexer #(.tristate("true"), .width(8)) demultiplexer_1 (
    .out0(out_36[7:0]), .out1(out_36[15:8]), .in(register_8_1_q1), .sel(in_24));
  register_z16bits register_z16bits_1 (
    .D1(out_36[0]), .D2(out_36[1]), .D3(out_36[2]), .D4(out_36[3]), .D5(out_36[4]), .D6(out_36[5]),
    .D7(out_36[6]), .D8(out_36[7]), .D9(out_36[8]), .D10(out_36[9]), .D11(out_36[10]), .D12(out_36[11]),
    .D13(out_36[12]), .D14(out_36[13]), .D15(out_36[14]), .D16(out_36[15]), .CLK(in_28), .LOAD1(in_29),
    .LOAD2(in_30), .EN1(in_31), .EN2(in_32), .Q1(out_36[0]), .Q2(out_36[1]), .Q3(out_36[2]), .Q4(out_36[3]),
    .Q5(out_36[4]), .Q6(out_36[5]), .Q7(out_36[6]), .Q8(out_36[7]), .Q9(out_36[8]), .Q10(out_36[9]),
    .Q11(out_36[10]), .Q12(out_36[11]), .Q13(out_36[12]), .Q14(out_36[13]), .Q15(out_36[14]), .Q16(out_36[15]));  // open: O1, O2, O3, O4, O5, O6, O7, O8, O9, O10, O11, O12, O13, O14, O15, O16
  register_8 register_8_2 (
    .D1(out_36[0]), .D2(out_36[1]), .D3(out_36[2]), .D4(out_36[3]), .D5(out_36[4]), .D6(out_36[5]),
    .D7(out_36[6]), .D8(out_36[7]), .LOAD(in_1), .CLK(in_2), .EN(in_3), .O1(register_8_2_o1[0]),
    .O2(register_8_2_o1[1]), .O3(register_8_2_o1[2]), .O4(register_8_2_o1[3]), .O5(register_8_2_o1[4]),
    .O6(register_8_2_o1[5]), .O7(register_8_2_o1[6]), .O8(register_8_2_o1[7]), .Q1(out_36[0]),
    .Q2(out_36[1]), .Q3(out_36[2]), .Q4(out_36[3]), .Q5(out_36[4]), .Q6(out_36[5]), .Q7(out_36[6]),
    .Q8(out_36[7]));
  register_8 register_8_3 (
    .D1(out_36[0]), .D2(out_36[1]), .D3(out_36[2]), .D4(out_36[3]), .D5(out_36[4]), .D6(out_36[5]),
    .D7(out_36[6]), .D8(out_36[7]), .LOAD(in_15), .CLK(in_16), .EN(in_17), .O1(register_8_3_o1[0]),
    .O2(register_8_3_o1[1]), .O3(register_8_3_o1[2]), .O4(register_8_3_o1[3]), .O5(register_8_3_o1[4]),
    .O6(register_8_3_o1[5]), .O7(register_8_3_o1[6]), .O8(register_8_3_o1[7]), .Q1(out_36[0]),
    .Q2(out_36[1]), .Q3(out_36[2]), .Q4(out_36[3]), .Q5(out_36[4]), .Q6(out_36[5]), .Q7(out_36[6]),
    .Q8(out_36[7]));
  register_8 register_8_4 (
    .D1(out_36[0]), .D2(out_36[1]), .D3(out_36[2]), .D4(out_36[3]), .D5(out_36[4]), .D6(out_36[5]),
    .D7(out_36[6]), .D8(out_36[7]), .LOAD(in_25), .CLK(in_26), .EN(in_27), .Q1(out_36[0]), .Q2(out_36[1]),
    .Q3(out_36[2]), .Q4(out_36[3]), .Q5(out_36[4]), .Q6(out_36[5]), .Q7(out_36[6]), .Q8(out_36[7]));  // open: O1, O2, O3, O4, O5, O6, O7, O8
  register_8 register_8_5 (
    .D1(out_36[0]), .D2(out_36[1]), .D3(out_36[2]), .D4(out_36[3]), .D5(out_36[4]), .D6(out_36[5]),
    .D7(out_36[6]), .D8(out_36[7]), .LOAD(in_33), .CLK(in_34), .EN(in_35), .Q1(out_36[0]), .Q2(out_36[1]),
    .Q3(out_36[2]), .Q4(out_36[3]), .Q5(out_36[4]), .Q6(out_36[5]), .Q7(out_36[6]), .Q8(out_36[7]));  // open: O1, O2, O3, O4, O5, O6, O7, O8
  // arithmetic_logic_unit arithmetic_logic_unit_1: pin names not known; wires that end beside it: register_8_2_o1, register_8_3_o1, in_8, in_9, arithmetic_logic_unit_1_p5, out_36[7:0], arithmetic_logic_unit_1_p7
  nor nor_1 (nor_1_out, out_36[0], out_36[1], out_36[2], out_36[3], out_36[4], out_36[5], out_36[6], out_36[7]);
  flags flags_1 (
    .Carry(arithmetic_logic_unit_1_p7), .Sign(arithmetic_logic_unit_1_p5), .Zero(nor_1_out), .LOAD(in_10),
    .CLK(in_11));  // open: Carry_out, Sign_out, Zero_out

  // Notes on the sheet:
  //   Random Access Memory
  //   Memory Address Register
  //   Memory Data Register
  //   Accumulator Register
  //   Temporary Register
  //   Register B
  //   Register C
endmodule
